# Fritzing sketch circuiyt (saved by Fritzing 0.9.3b)
breadboards: 1

parts:
  Composant1 = Arduino Mega 2560 (Rev3)
  R1 = Temperature Sensor (Thermistor) [thermistor_type=NTC package=THT]
  Q1 = NPN-Transistor [package="TO92 [THT]"]
  Q2 = NPN-Transistor [package="TO92 [THT]"]
  Q3 = NPN-Transistor [package="TO92 [THT]"]
  Q4 = NPN-Transistor [package="TO92 [THT]"]
  LED1 = 5641AS-1 [part_number=5641AS-1 package="DIP (Dual Inline) [THT]"]
  R2 = Resistor [tolerance=±5% resistance=220 package=THT]
  R4 = Resistor [tolerance=±5% resistance=220 package=THT]
  R5 = Resistor [tolerance=±5% resistance=220 package=THT]
  R6 = Resistor [tolerance=±5% resistance=220 package=THT]
  R7 = Resistor [tolerance=±5% resistance=220 package=THT]
  R8 = Resistor [tolerance=±5% resistance=220 package=THT]
  R9 = Resistor [tolerance=±5% resistance=220 package=THT]
  R10 = Resistor [tolerance=±5% resistance=220 package=THT]
  R11 = Resistor [tolerance=±5% resistance=10k package=THT]

nets:
  N1: Composant1.A0, R1.pin_0, R11.Pin_1
  N2: Composant1.D12_PWM, R10.Pin_1
  N3: Composant1.D11_PWM, R6.Pin_1
  N4: Composant1.D10_PWM, R4.Pin_1
  N5: Composant1.D9_PWM, R5.Pin_1
  N6: Composant1.5V, R1.pin_1
  N7: Composant1.D22, LED1.anA
  N8: Composant1.D23, LED1.anB
  N9: Composant1.D24, LED1.anC
  N10: Composant1.D25, LED1.anD
  N11: Composant1.D26, LED1.anE
  N12: Composant1.D27, LED1.anF
  N13: Composant1.D28, LED1.anG
  N14: Composant1.D29, LED1.anDP
  N15: Q1.E, R7.Pin_1
  N16: Q1.B, R10.Pin_0
  N17: Q1.C, LED1.cat1
  N18: Q2.E, R8.Pin_1
  N19: Q2.B, R6.Pin_0
  N20: Q2.C, LED1.cat2
  N21: Q3.E, R9.Pin_1
  N22: Q3.B, R4.Pin_0
  N23: Q3.C, LED1.cat3
  N24: Q4.E, R2.Pin_1
  N25: Q4.B, R5.Pin_0
  N26: Q4.C, LED1.cat4
  N27: R2.Pin_0, R7.Pin_0, R8.Pin_0, R9.Pin_0, R11.Pin_0

custom parts:
  5641AS-1: 4 digit 7 segment common cathode LED display

// code stored in the sketch: 4digits.ino
#include "fonction.h"
#define tempPin A0

int uni = 0;
int dix = 0;
int cent = 0;
int mil = 0;

void setup() {
  pinMode(pinA, OUTPUT);
  pinMode(pinB, OUTPUT);
  pinMode(pinC, OUTPUT);
  pinMode(pinD, OUTPUT);
  pinMode(pinE, OUTPUT);
  pinMode(pinF, OUTPUT);
  pinMode(pinG, OUTPUT);
  pinMode(pinDP, OUTPUT);
  pinMode(D1, OUTPUT);
  pinMode(D2, OUTPUT);
  pinMode(D3, OUTPUT);
  pinMode(D4, OUTPUT);
}

void loop() {
  int tempReading = analogRead(tempPin);
  double tempK = log(10000.0 * ((1024.0 / tempReading - 1)));
  tempK = 1 / (0.001129148 + (0.000234125 + (0.0000000876741 * tempK * tempK )) * tempK );
  float tempC = tempK - 273.15;

  int absTempC = abs(tempC);
  show_num('c',4,false,1,0,0,1,1,1,0);
  show_num('c',3,false,1,1,0,0,0,1,1);
  show_num((absTempC%10),2);
  show_num((absTempC/10),1);
}
